// Logisim project Project.circ as structural Verilog: 19 circuits, main circuit main
module main (
  input  [3:0] INPR
);

  wire and_1_out, clock_1_out, main_control_1_dr_ld, main_control_1_e_clr, main_control_1_hlt,
       main_control_1_outr__ld;
  wire [1:0] main_control_1_ir__ld_bus, main_control_1_m_ar___ld_bus;
  wire [2:0] main_control_1_ar__ld_inc_bus, main_control_1_pc__ld_inc_bus;
  wire [3:0] AC_output, AR_output, controlled_buffer_1_out, controlled_buffer_1_out_2, DR_output, IR_output,
       IR_output_2, main_control_1_ac__ld_inc_clr_bus, n4xalu_1_output_ac, OUTR_output, PC_output;
  wire [6:0] main_control_1_alu;
  wire [7:0] ram_1_data;

  Main_Control main_control_1 (
    .IR_4_7(IR_output_2), .CLK(and_1_out), .M_AR___LD_BUS(main_control_1_m_ar___ld_bus),
    .AR__LD_INC_BUS(main_control_1_ar__ld_inc_bus), .PC__LD_INC_BUS(main_control_1_pc__ld_inc_bus),
    .DR_LD(main_control_1_dr_ld), .AC__LD_INC_CLR_BUS(main_control_1_ac__ld_inc_clr_bus),
    .IR__LD_BUS(main_control_1_ir__ld_bus), .OUTR__LD(main_control_1_outr__ld), .ALU(main_control_1_alu),
    .HLT(main_control_1_hlt), .E_CLR(main_control_1_e_clr));
  Clock clock_1 (.out(clock_1_out));
  and and_1 (and_1_out, ~main_control_1_hlt, clock_1_out);  // AND_Gate
  _4xALU u_4xalu_1 (
    .AC(AC_output), .DR(DR_output), .INPR(INPR), .AND(main_control_1_alu[0]), .ADD(main_control_1_alu[1]),
    .CMA(main_control_1_alu[2]), .LD_DR(main_control_1_alu[3]), .LD_INPR(main_control_1_alu[4]),
    .CIR(main_control_1_alu[5]), .CIL(main_control_1_alu[6]), .Cin(1'b0), .E_AC_0(1'b0),
    .E_AC_3(main_control_1_e_clr), .output_AC(n4xalu_1_output_ac));  // open: Cout
  _4_BIT_REGISTER AR (
    .INPUT(controlled_buffer_1_out), .CLK(and_1_out), .LD(main_control_1_ar__ld_inc_bus[0]),
    .INC(main_control_1_ar__ld_inc_bus[1]), .OUTPUT(AR_output));  // open: CLR
  // Probe on PC_output
  _4_BIT_REGISTER PC (
    .INPUT(controlled_buffer_1_out), .CLK(and_1_out), .LD(main_control_1_pc__ld_inc_bus[0]),
    .INC(main_control_1_pc__ld_inc_bus[1]), .OUTPUT(PC_output));  // open: CLR
  _4_BIT_REGISTER DR (
    .INPUT(controlled_buffer_1_out), .CLK(and_1_out), .LD(main_control_1_dr_ld), .OUTPUT(DR_output));  // open: INC, CLR
  _4_BIT_REGISTER AC (
    .INPUT(n4xalu_1_output_ac), .CLK(and_1_out), .LD(main_control_1_ac__ld_inc_clr_bus[0]),
    .INC(main_control_1_ac__ld_inc_clr_bus[1]), .CLR(main_control_1_ac__ld_inc_clr_bus[2]), .OUTPUT(AC_output));
  // Probe on {IR_output_2, IR_output}
  _8_BIT_REGISTER IR (
    .Input({controlled_buffer_1_out_2, controlled_buffer_1_out}), .CLK(and_1_out),
    .LD(main_control_1_ir__ld_bus[0]), .Output({IR_output_2, IR_output}));
  _4_BIT_REGISTER OUTR (
    .INPUT(controlled_buffer_1_out), .CLK(and_1_out), .LD(main_control_1_outr__ld), .OUTPUT(OUTR_output));  // open: INC, CLR
  RAM #(.addrWidth(4), .bus("separate")) ram_1 (
    .addr(AR_output), .din({controlled_buffer_1_out_2, controlled_buffer_1_out}), .data(ram_1_data),
    .str(main_control_1_m_ar___ld_bus[0]), .clk(and_1_out));  // open: sel, ld, clr
  // Probe on AR_output
  // Probe on DR_output
  // Probe on AC_output
  // Probe on OUTR_output
  assign {controlled_buffer_1_out_2, controlled_buffer_1_out} = main_control_1_m_ar___ld_bus[1] ? ram_1_data : 8'bz;  // Controlled_Buffer controlled_buffer_1
  assign {controlled_buffer_1_out_2, controlled_buffer_1_out} = main_control_1_ar__ld_inc_bus[2] ? {4'b0000, AR_output} : 8'bz;  // Controlled_Buffer controlled_buffer_2
  assign {controlled_buffer_1_out_2, controlled_buffer_1_out} = main_control_1_pc__ld_inc_bus[2] ? {4'b0000, PC_output} : 8'bz;  // Controlled_Buffer controlled_buffer_3
  assign {controlled_buffer_1_out_2, controlled_buffer_1_out} = main_control_1_ac__ld_inc_clr_bus[3] ? {4'b0000, AC_output} : 8'bz;  // Controlled_Buffer controlled_buffer_4
  assign {controlled_buffer_1_out_2, controlled_buffer_1_out} = main_control_1_ir__ld_bus[1] ? {IR_output_2, IR_output} : 8'bz;  // Controlled_Buffer controlled_buffer_5
endmodule

module Main_Control (
  input  [3:0] IR_4_7,
  input  CLK,
  output [1:0] M_AR___LD_BUS,
  output [2:0] AR__LD_INC_BUS,
  output [2:0] PC__LD_INC_BUS,
  output DR_LD,
  output [3:0] AC__LD_INC_CLR_BUS,
  output [1:0] IR__LD_BUS,
  output OUTR__LD,
  output [6:0] ALU,
  output HLT,
  output E_CLR
);

  wire decoder_1_out15, sc_clr_1_out_18;
  wire [3:0] counter_1_out_3;
  wire [4:0] decoder_2_out0;
  wire [6:0] decoder_1_out13;
  wire [14:3] decoder_1_out3;

  SC_CLR sc_clr_1 (
    .T3(decoder_2_out0[3]), .T4(decoder_2_out0[4]), .D0(decoder_1_out13[6]), .D1(decoder_1_out13[5]),
    .D2(decoder_1_out13[4]), .D3(decoder_1_out3[3]), .D4(decoder_1_out3[4]), .D5(decoder_1_out3[5]),
    .D6(decoder_1_out3[6]), .D7(decoder_1_out3[7]), .D8(decoder_1_out3[8]), .D9(decoder_1_out13[3]),
    .D10(decoder_1_out3[10]), .D11(decoder_1_out13[2]), .D12(decoder_1_out13[1]), .D13(decoder_1_out13[0]),
    .D14(decoder_1_out3[14]), .out_18(sc_clr_1_out_18));
  COUNTER counter_1 (.in_1(CLK), .SC_CLR(sc_clr_1_out_18), .out_3(counter_1_out_3));
  Decoder #(.select(4)) decoder_1 (
    .out0(decoder_1_out13[6]), .out1(decoder_1_out13[5]), .out2(decoder_1_out13[4]),
    .out3(decoder_1_out3[3]), .out4(decoder_1_out3[4]), .out5(decoder_1_out3[5]), .out6(decoder_1_out3[6]),
    .out7(decoder_1_out3[7]), .out8(decoder_1_out3[8]), .out9(decoder_1_out13[3]),
    .out10(decoder_1_out3[10]), .out11(decoder_1_out13[2]), .out12(decoder_1_out13[1]),
    .out13(decoder_1_out13[0]), .out14(decoder_1_out3[14]), .out15(decoder_1_out15), .sel(IR_4_7));  // open: en
  Decoder #(.select(4)) decoder_2 (
    .out0(decoder_2_out0[0]), .out1(decoder_2_out0[1]), .out2(decoder_2_out0[2]), .out3(decoder_2_out0[3]),
    .out4(decoder_2_out0[4]), .sel(counter_1_out_3));  // open: out5, out6, out7, out8, out9, out10, out11, out12, out13, out14, out15, en
  and and_1 (HLT, decoder_1_out15, decoder_2_out0[3]);
  and and_2 (E_CLR, decoder_2_out0[3], decoder_1_out3[8]);
  REGISTER_control register_control_1 (
    .T0(decoder_2_out0[0]), .T1(decoder_2_out0[1]), .T2(decoder_2_out0[2]), .T3(decoder_2_out0[3]),
    .T4(decoder_2_out0[4]), .D0(decoder_1_out13[6]), .D1(decoder_1_out13[5]), .D2(decoder_1_out13[4]),
    .D3(decoder_1_out3[3]), .D4(decoder_1_out3[4]), .D5(decoder_1_out3[5]), .D6(decoder_1_out3[6]),
    .D7(decoder_1_out3[7]), .D8(decoder_1_out3[8]), .D9(decoder_1_out13[3]), .D10(decoder_1_out3[10]),
    .D11(decoder_1_out13[2]), .D12(decoder_1_out13[1]), .D13(decoder_1_out13[0]), .D14(decoder_1_out3[14]),
    .out_21(M_AR___LD_BUS), .out_22(AR__LD_INC_BUS), .out_23(PC__LD_INC_BUS), .out_24(DR_LD),
    .out_25(AC__LD_INC_CLR_BUS), .out_26(IR__LD_BUS), .out_27(OUTR__LD));
  ALU_control alu_control_1 (
    .T3(decoder_2_out0[3]), .T4(decoder_2_out0[4]), .D0(decoder_1_out13[6]), .D1(decoder_1_out13[5]),
    .D2(decoder_1_out13[4]), .D9(decoder_1_out13[3]), .D11(decoder_1_out13[2]), .D12(decoder_1_out13[1]),
    .D13(decoder_1_out13[0]), .AND(ALU[0]), .ADD(ALU[1]), .CMA(ALU[2]), .LD_DR(ALU[3]), .LD_INPR(ALU[4]),
    .CIR(ALU[5]), .CIL(ALU[6]));

  // Notes on the sheet:
  //   T(3_4)
  //   D(0_14)
  //   D(0-15)
  //   T(0_4)
  //   T(0_4)
  //   T(3_4)
  //   D(0_14)
endmodule

// REGISTER CONTROL
module REGISTER_control (
  input  T0,
  input  T1,
  input  T2,
  input  T3,
  input  T4,
  input  D0,
  input  D1,
  input  D2,
  input  D3,
  input  D4,
  input  D5,
  input  D6,
  input  D7,
  input  D8,
  input  D9,
  input  D10,
  input  D11,
  input  D12,
  input  D13,
  input  D14,
  output [1:0] out_21,
  output [2:0] out_22,
  output [2:0] out_23,
  output out_24,
  output [3:0] out_25,
  output [1:0] out_26,
  output out_27
);

  M_AR__control m_ar__control_1 (
    .D0(D0), .D1(D1), .D2(D2), .D3(D3), .D5(D5), .D6(D6), .T1(T1), .T3(T3), .M_AR__LD(out_21[0]),
    .M_AR__BUS(out_21[1]));
  AR_control ar_control_1 (
    .D4(D4), .D5(D5), .T0(T0), .T2(T2), .T3(T3), .T4(T4), .AR_LD(out_22[0]), .AR_INR(out_22[1]),
    .AR_BUS(out_22[2]));
  PC_control pc_control_1 (
    .T0(T0), .T1(T1), .T3(T2), .T4(T3), .D4(D4), .D5(D5), .D6(D6), .PC_LD(out_23[0]), .PC_INC(out_23[1]),
    .PC_BUS(out_23[2]));
  DR_control dr_control_1 (.D0(D0), .D1(D1), .D2(D2), .T3(T3), .DR_LD(out_24));
  IR_control ir_control_1 (.IR_LD(out_26[0]), .IR_BUS(out_26[1]), .T1(T1), .T2(T2));
  OUTR_control outr_control_1 (.LD_OUTR(out_27), .D14(D14), .T3(T3));
  AC_control ac_control_1 (
    .D0(D0), .D1(D1), .D2(D2), .D3(D3), .D7(D7), .D9(D9), .D10(D10), .D11(D11), .D12(D12), .D13(D13),
    .D14(D14), .T3(T3), .T4(T4), .AC_LD(out_25[0]), .AC_INR(out_25[1]), .AC_CLR(out_25[2]), .AC_BUS(out_25[3]));
endmodule

module SC_CLR (
  input  T3,
  input  T4,
  input  D0,
  input  D1,
  input  D2,
  input  D3,
  input  D4,
  input  D5,
  input  D6,
  input  D7,
  input  D8,
  input  D9,
  input  D10,
  input  D11,
  input  D12,
  input  D13,
  input  D14,
  output out_18
);

  wire and_1_out, and_2_out, and_3_out, and_4_out, and_5_out, and_6_out, and_7_out, and_8_out, and_9_out,
       and_10_out, and_11_out, and_12_out, and_13_out, and_14_out, and_15_out;

  and and_1 (and_1_out, D0, T4);
  and and_2 (and_2_out, D1, T4);
  and and_3 (and_3_out, D2, T4);
  and and_4 (and_4_out, D3, T3);
  and and_5 (and_5_out, D4, T3);
  and and_6 (and_6_out, D5, T4);
  and and_7 (and_7_out, D6, T3);
  and and_8 (and_8_out, D7, T3);
  and and_9 (and_9_out, D8, T3);
  and and_10 (and_10_out, D9, T3);
  and and_11 (and_11_out, D10, T3);
  and and_12 (and_12_out, D11, T3);
  and and_13 (and_13_out, D12, T3);
  and and_14 (and_14_out, D13, T3);
  and and_15 (and_15_out, D14, T3);
  or or_1 (out_18, and_1_out, and_2_out, and_3_out, and_4_out, and_5_out, and_6_out, and_7_out, and_8_out, and_9_out, and_10_out, and_11_out, and_12_out, and_13_out, and_14_out, and_15_out);
endmodule

module COUNTER (
  input  in_1,
  input  SC_CLR,
  output [3:0] out_3
);

  wire d_ff_1_q;

  Counter #(.width(4), .max('hf)) counter_1 (.Q(out_3), .clk(in_1), .clr(d_ff_1_q));  // open: load, D, count, carry
  D_Flip_Flop d_ff_1 (.clk(in_1), .D(SC_CLR), .Q(d_ff_1_q));  // open: Qn, preset, en, reset
endmodule

// PC
module PC_control (
  input  T0,
  input  T1,
  input  T3,
  input  T4,
  input  D4,
  input  D5,
  input  D6,
  output PC_LD,
  output PC_INC,
  output PC_BUS
);

  wire and_1_out, and_2_out, and_3_out, or_1_out;

  or or_1 (or_1_out, D6, D4);
  and and_1 (and_1_out, or_1_out, T3);
  or or_2 (PC_LD, and_1_out, and_2_out);
  and and_2 (and_2_out, D5, T4);
  and and_3 (and_3_out, D5, T3);
  or or_3 (PC_BUS, and_3_out, T0);

  assign PC_INC = T1;
endmodule

// AR
module AR_control (
  input  D4,
  input  D5,
  input  T0,
  input  T2,
  input  T3,
  input  T4,
  output AR_LD,
  output AR_INR,
  output AR_BUS
);

  wire and_1_out, and_2_out;

  and and_1 (and_1_out, D4, T3);
  and and_2 (and_2_out, D5, T4);
  or or_1 (AR_LD, T0, T2);
  and and_3 (AR_INR, D5, T3);
  or or_2 (AR_BUS, and_1_out, and_2_out);
endmodule

// AC
module AC_control (
  input  D0,
  input  D1,
  input  D2,
  input  D3,
  input  D7,
  input  D9,
  input  D10,
  input  D11,
  input  D12,
  input  D13,
  input  D14,
  input  T3,
  input  T4,
  output AC_LD,
  output AC_INR,
  output AC_CLR,
  output AC_BUS
);

  wire ADD_out, AND_out, AR_out, COM_out, DR_out, INPR_out, OUTR_out, SHL_out, SHR_out;

  and AND (AND_out, D0, T4);
  and ADD (ADD_out, D1, T4);
  and DR (DR_out, D2, T4);
  and INPR (INPR_out, D13, T3);
  and COM (COM_out, D9, T3);
  and SHR (SHR_out, D11, T3);
  and SHL (SHL_out, D12, T3);
  and INC (AC_INR, D10, T3);
  and CLR (AC_CLR, D7, T3);
  and AR (AR_out, D3, T3);
  and OUTR (OUTR_out, D14, T3);
  or or_1 (AC_BUS, AR_out, OUTR_out);
  or or_2 (AC_LD, AND_out, ADD_out, DR_out, INPR_out, COM_out, SHR_out, SHL_out);
endmodule

// DR
module DR_control (
  input  D0,
  input  D1,
  input  D2,
  input  T3,
  output DR_LD
);

  wire and_1_out, and_2_out, and_3_out;

  and and_1 (and_1_out, D0, T3);
  and and_2 (and_2_out, D1, T3);
  and and_3 (and_3_out, T3, D2);
  or or_1 (DR_LD, and_1_out, and_3_out, and_2_out);
endmodule

// OUTR
module OUTR_control (
  input  D14,
  input  T3,
  output LD_OUTR
);

  and AC (LD_OUTR, D14, T3);
endmodule

// IR
module IR_control (
  input  T1,
  input  T2,
  output IR_LD,
  output IR_BUS
);


  assign IR_BUS = T2;
  assign IR_LD = T1;
endmodule

// M[AR]
module M_AR__control (
  input  D0,
  input  D1,
  input  D2,
  input  D3,
  input  D5,
  input  D6,
  input  T1,
  input  T3,
  output M_AR__LD,
  output M_AR__BUS
);

  wire and_1_out, and_2_out, and_3_out, and_4_out, and_5_out, and_6_out;

  and and_1 (and_1_out, D3, T3);
  and and_2 (and_2_out, D5, T3);
  and and_3 (and_3_out, D0, T3);
  and and_4 (and_4_out, D1, T3);
  and and_5 (and_5_out, D2, T3);
  and and_6 (and_6_out, D6, T3);
  or or_1 (M_AR__LD, and_1_out, and_2_out);
  or or_2 (M_AR__BUS, and_3_out, and_4_out, T1, and_5_out, and_6_out);
endmodule

// ALU CONTROL
module ALU_control (
  input  T3,
  input  T4,
  input  D0,
  input  D1,
  input  D2,
  input  D9,
  input  D11,
  input  D12,
  input  D13,
  output AND,
  output ADD,
  output CMA,
  output LD_DR,
  output LD_INPR,
  output CIR,
  output CIL
);

  and and_1 (AND, D0, T4);
  and and_2 (ADD, D1, T4);
  and and_3 (CMA, D9, T3);
  and and_4 (LD_DR, D2, T4);
  and and_5 (LD_INPR, D13, T3);
  and and_6 (CIR, D11, T3);
  and and_7 (CIL, D12, T3);
endmodule

module _8_BIT_REGISTER (
  input  [7:0] Input,
  input  CLK,
  input  LD,
  output [7:0] Output
);

  _4_BIT_REGISTER u_4_bit_register_1 (.INPUT(Input[3:0]), .CLK(CLK), .LD(LD), .OUTPUT(Output[3:0]));  // open: INC, CLR
  _4_BIT_REGISTER u_4_bit_register_2 (.INPUT(Input[7:4]), .CLK(CLK), .LD(LD), .OUTPUT(Output[7:4]));  // open: INC, CLR
endmodule

module _4_BIT_REGISTER (
  input  INC,
  input  LD,
  input  [3:0] INPUT,
  input  CLK,
  input  CLR,
  output [3:0] OUTPUT
);

  wire and_1_out, and_2_out, and_3_out, and_4_out, and_5_out, and_6_out, and_7_out, and_8_out, and_9_out,
       and_10_out, and_11_out, and_12_out, not_1_out, not_2_out, not_3_out, not_4_out, not_5_out, not_6_out,
       or_1_out, or_2_out, or_3_out, or_4_out, or_5_out, or_6_out, or_7_out, or_8_out;

  not not_1 (not_1_out, LD);
  not not_2 (not_2_out, INPUT[3]);
  and and_1 (and_1_out, INC, not_1_out);
  not not_3 (not_3_out, not_1_out);
  not not_4 (not_4_out, INPUT[0]);
  not not_5 (not_5_out, INPUT[1]);
  not not_6 (not_6_out, INPUT[2]);
  and and_2 (and_2_out, not_3_out, INPUT[0]);
  and and_3 (and_3_out, not_3_out, not_4_out);
  and and_4 (and_4_out, not_3_out, INPUT[1]);
  and and_5 (and_5_out, not_3_out, not_5_out);
  and and_6 (and_6_out, not_3_out, INPUT[2]);
  and and_7 (and_7_out, not_3_out, not_6_out);
  and and_8 (and_8_out, not_3_out, INPUT[3]);
  and and_9 (and_9_out, not_3_out, not_2_out);
  and and_10 (and_10_out, OUTPUT[0], and_1_out);
  and and_11 (and_11_out, and_1_out, OUTPUT[0], OUTPUT[1]);
  and and_12 (and_12_out, and_1_out, OUTPUT[0], OUTPUT[1], OUTPUT[2]);
  or or_1 (or_1_out, and_2_out, and_1_out);
  or or_2 (or_2_out, and_3_out, and_1_out);
  or or_3 (or_3_out, and_4_out, and_10_out);
  or or_4 (or_4_out, and_10_out, and_5_out);
  or or_5 (or_5_out, and_6_out, and_11_out);
  or or_6 (or_6_out, and_11_out, and_7_out);
  or or_7 (or_7_out, and_8_out, and_12_out);
  or or_8 (or_8_out, and_12_out, and_9_out);
  J_K_Flip_Flop j_k_ff_1 (.J(or_1_out), .clk(CLK), .K(or_2_out), .Q(OUTPUT[0]), .reset(CLR));  // open: Qn, preset, en
  J_K_Flip_Flop j_k_ff_2 (.J(or_3_out), .clk(CLK), .K(or_4_out), .Q(OUTPUT[1]), .reset(CLR));  // open: Qn, preset, en
  J_K_Flip_Flop j_k_ff_3 (.J(or_5_out), .clk(CLK), .K(or_6_out), .Q(OUTPUT[2]), .reset(CLR));  // open: Qn, preset, en
  J_K_Flip_Flop j_k_ff_4 (.J(or_7_out), .clk(CLK), .K(or_8_out), .Q(OUTPUT[3]), .reset(CLR));  // open: Qn, preset, en
endmodule

// ALU
module _4xALU (
  input  Cin,
  input  E_AC_0,
  input  [3:0] AC,
  input  [3:0] DR,
  input  [3:0] INPR,
  input  AND,
  input  ADD,
  input  CMA,
  input  LD_DR,
  input  LD_INPR,
  input  CIR,
  input  CIL,
  input  E_AC_3,
  output [3:0] output_AC,
  output Cout
);

  wire n1xalu_1_out_14, n1xalu_2_out_14, n1xalu_3_out_14;

  _1xALU u_1xalu_1 (
    .AND(AND), .ADD(ADD), .CMA(CMA), .LD_DR(LD_DR), .LD_INPR(LD_INPR), .CIR(CIR), .CIL(CIL), .AC_i_1(E_AC_0),
    .AC_i_1_2(AC[1]), .INPR(INPR[0]), .DR(DR[0]), .AC(AC[0]), .in_6(Cin), .out_14(n1xalu_1_out_14),
    .output_AC(output_AC[0]));
  _1xALU u_1xalu_2 (
    .AND(AND), .ADD(ADD), .CMA(CMA), .LD_DR(LD_DR), .LD_INPR(LD_INPR), .CIR(CIR), .CIL(CIL), .AC_i_1(AC[0]),
    .AC_i_1_2(AC[2]), .INPR(INPR[1]), .DR(DR[1]), .AC(AC[1]), .in_6(n1xalu_1_out_14),
    .out_14(n1xalu_2_out_14), .output_AC(output_AC[1]));
  _1xALU u_1xalu_3 (
    .AND(AND), .ADD(ADD), .CMA(CMA), .LD_DR(LD_DR), .LD_INPR(LD_INPR), .CIR(CIR), .CIL(CIL), .AC_i_1(AC[1]),
    .AC_i_1_2(AC[3]), .INPR(INPR[2]), .DR(DR[2]), .AC(AC[2]), .in_6(n1xalu_2_out_14),
    .out_14(n1xalu_3_out_14), .output_AC(output_AC[2]));
  _1xALU u_1xalu_4 (
    .AND(AND), .ADD(ADD), .CMA(CMA), .LD_DR(LD_DR), .LD_INPR(LD_INPR), .CIR(CIR), .CIL(CIL), .AC_i_1(AC[2]),
    .AC_i_1_2(E_AC_3), .INPR(INPR[3]), .DR(DR[3]), .AC(AC[3]), .in_6(n1xalu_3_out_14), .out_14(Cout),
    .output_AC(output_AC[3]));

  // Notes on the sheet:
  //   AC(0)
  //   AC(1)
  //   AC(2)
  //   AC(3)
endmodule

module _1xALU (
  input  INPR,
  input  DR,
  input  AC,
  input  AND,
  input  ADD,
  input  in_6,
  input  CMA,
  input  LD_DR,
  input  LD_INPR,
  input  CIR,
  input  CIL,
  input  AC_i_1,
  input  AC_i_1_2,
  output out_14,
  output output_AC
);

  wire add_out, adder_1_out, and_out, comp_out, Id_DR_out, Id_INPR_out, not_1_out, shl_out, shr_out;

  Adder #(.width(1)) adder_1 (.a(AC), .b(DR), .out(adder_1_out), .cin(in_6), .cout(out_14));
  not not_1 (not_1_out, AC);
  and u_and (and_out, AND, AC, DR);
  and u_add (add_out, ADD, adder_1_out);
  and comp (comp_out, CMA, not_1_out);
  and Id_DR (Id_DR_out, LD_DR, DR);
  and Id_INPR (Id_INPR_out, LD_INPR, INPR);
  and shr (shr_out, CIR, AC_i_1_2);
  and shl (shl_out, CIL, AC_i_1);
  or or_1 (output_AC, and_out, add_out, comp_out, Id_DR_out, Id_INPR_out, shr_out, shl_out);
endmodule

module control (
  input  C1,
  input  C2,
  output Q1,
  output Q2,
  output Q3
);

  and and_1 (Q1, ~C1, ~C2);  // AND_Gate
  and and_2 (Q2, ~C1, C2);  // AND_Gate
  and and_3 (Q3, C1, ~C2);  // AND_Gate
endmodule

module Bus_control (
  input  in_1,
  input  in_2
);

  wire clock_1_out, control_1_q1, control_1_q2, control_1_q3;
  wire [3:0] controlled_buffer_1_out, R1_output, R2_output, R3_output;

  Clock clock_1 (.out(clock_1_out));
  control control_1 (.C1(in_1), .C2(in_2), .Q1(control_1_q1), .Q2(control_1_q2), .Q3(control_1_q3));
  // Probe on R1_output
  _4_BIT_REGISTER R1 (
    .INPUT(controlled_buffer_1_out), .CLK(clock_1_out), .LD(control_1_q1), .OUTPUT(R1_output));  // open: INC, CLR
  // Probe on R2_output
  _4_BIT_REGISTER R2 (
    .INPUT(controlled_buffer_1_out), .CLK(clock_1_out), .LD(control_1_q2), .OUTPUT(R2_output));  // open: INC, CLR
  // Probe on R3_output
  _4_BIT_REGISTER R3 (
    .INPUT(controlled_buffer_1_out), .CLK(clock_1_out), .LD(control_1_q3), .OUTPUT(R3_output));  // open: INC, CLR
  assign controlled_buffer_1_out = control_1_q3 ? R1_output : 4'bz;  // Controlled_Buffer controlled_buffer_1
  assign controlled_buffer_1_out = control_1_q1 ? R2_output : 4'bz;  // Controlled_Buffer controlled_buffer_2
  assign controlled_buffer_1_out = control_1_q2 ? R3_output : 4'bz;  // Controlled_Buffer controlled_buffer_3
  // Probe on controlled_buffer_1_out
endmodule
